# Fritzing sketch neopixel24clock (saved by Fritzing 0.9.2b)

parts:
  Part1 = Pro Trinket 5V
  neopixel1 = Neopixel 24 Ring
  Part2 = Real Time Clock Module - DS1307 RTC Breakout Board

nets:
  GND: Part1.GND, neopixel1.GND, Part2.GND
  +5V: Part1.+5V, neopixel1.Vcc, Part2.5V
  N1: Part1.D12, neopixel1.IN
  N2: Part1.A4, Part2.SDA
  N3: Part1.A5, Part2.SCL

custom parts:
  Pro Trinket 5V: The Pro Trinket 5V is like an Arduino Pro Mini with more pins and USB included. Built with the common core Arduino chip, the ATmega328p, it has 18 GPIO, 2 extra analog inputs, 28K of flash, and 2K of RAM. It has onboard USB bootloading support with Optiboot support, so you can either program your Pro Trinket over USB or with a FTDI cable. The Pro Trinket is programmable using the Arduino IDE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
